// Logisim project MAIN.circ as structural Verilog: 1 circuit, main circuit main
module main (
  input  in_1,
  input  in_2
);

  wire and_1_out, and_2_out, and_3_out, and_4_out, and_5_out, and_6_out, and_7_out, and_8_out, and_9_out,
       and_10_out, and_11_out, and_12_out, and_13_out, and_14_out, and_15_out, and_16_out, and_17_out,
       and_18_out, and_19_out, and_20_out, and_21_out, and_22_out, and_23_out, clock_1_out, comparator_1_gt,
       comparator_1_lt, comparator_2_gt, comparator_3_gt, comparator_4_gt, comparator_5_gt, comparator_6_gt,
       comparator_7_gt, comparator_8_gt, comparator_9_gt, comparator_10_gt, comparator_11_gt,
       comparator_12_gt, comparator_13_gt, comparator_14_gt, comparator_15_gt, comparator_16_gt, not_1_out,
       not_2_out, not_3_out, not_4_out, not_5_out, not_6_out, not_7_out, not_8_out, not_9_out, not_10_out,
       not_11_out, not_12_out, not_13_out, not_14_out, not_15_out, not_16_out, or_1_out, or_2_out, or_3_out,
       or_4_out, or_5_out, or_6_out, or_7_out, or_8_out, or_9_out, or_10_out, or_11_out, or_12_out,
       or_13_out, or_14_out, or_15_out;
  wire [3:0] random_1_out;
  wire [5:0] random_2_out;

  and and_1 (and_1_out, not_6_out, not_5_out);
  Random #(.width(4)) random_1 (.clk(clock_1_out), .next(in_2), .out(random_1_out));  // open: clr
  Comparator #(.width(4), .mode("unsigned")) comparator_1 (
    .a(4'b0000), .b(random_1_out), .gt(comparator_1_gt), .lt(comparator_1_lt));  // open: eq
  Comparator #(.width(4), .mode("unsigned")) comparator_2 (
    .a(random_1_out), .b(4'b0101), .gt(comparator_2_gt));  // open: eq, lt
  Comparator #(.width(4), .mode("unsigned")) comparator_3 (
    .a(4'b0110), .b(random_1_out), .gt(comparator_3_gt));  // open: eq, lt
  Comparator #(.width(4), .mode("unsigned")) comparator_4 (
    .a(random_1_out), .b(4'b1010), .gt(comparator_4_gt));  // open: eq, lt
  Comparator #(.width(4), .mode("unsigned")) comparator_5 (
    .a(4'b1011), .b(random_1_out), .gt(comparator_5_gt));  // open: eq, lt
  Comparator #(.width(4), .mode("unsigned")) comparator_6 (
    .a(random_1_out), .b(4'b1111), .gt(comparator_6_gt));  // open: eq, lt
  and and_2 (and_2_out, not_4_out, not_3_out);
  not not_1 (not_1_out, comparator_1_gt);
  not not_2 (not_2_out, comparator_2_gt);
  not not_3 (not_3_out, comparator_3_gt);
  not not_4 (not_4_out, comparator_4_gt);
  not not_5 (not_5_out, comparator_5_gt);
  not not_6 (not_6_out, comparator_6_gt);
  and and_3 (and_3_out, not_2_out, not_1_out);
  not not_7 (not_7_out, comparator_7_gt);
  Comparator #(.width(6), .mode("unsigned")) comparator_7 (
    .a({6{1'b0}}), .b(random_2_out), .gt(comparator_7_gt));  // open: eq, lt
  not not_8 (not_8_out, comparator_8_gt);
  Comparator #(.width(6), .mode("unsigned")) comparator_8 (
    .a(random_2_out), .b(6'b010011), .gt(comparator_8_gt));  // open: eq, lt
  and and_4 (and_4_out, not_8_out, not_7_out);
  and and_5 (and_5_out, and_3_out, and_13_out);
  Comparator #(.width(6), .mode("unsigned")) comparator_9 (
    .a(6'b010100), .b(random_2_out), .gt(comparator_9_gt));  // open: eq, lt
  Comparator #(.width(6), .mode("unsigned")) comparator_10 (
    .a(random_2_out), .b(6'b100111), .gt(comparator_10_gt));  // open: eq, lt
  and and_6 (and_6_out, and_2_out, and_13_out);
  or or_1 (or_1_out, and_6_out, and_14_out);
  or or_2 (or_2_out, and_14_out, and_11_out);
  and and_7 (and_7_out, and_4_out, and_1_out);
  and and_8 (and_8_out, and_4_out, and_2_out);
  and and_9 (and_9_out, and_4_out, and_3_out);
  not not_9 (not_9_out, comparator_9_gt);
  not not_10 (not_10_out, comparator_10_gt);
  and and_10 (and_10_out, not_10_out, not_9_out);
  and and_11 (and_11_out, and_1_out, and_13_out);
  or or_3 (or_3_out, and_5_out, and_14_out);
  Comparator #(.width(6), .mode("unsigned")) comparator_11 (
    .a(6'b101000), .b(random_2_out), .gt(comparator_11_gt));  // open: eq, lt
  Comparator #(.width(6), .mode("unsigned")) comparator_12 (
    .a(random_2_out), .b(6'b110011), .gt(comparator_12_gt));  // open: eq, lt
  or or_4 (or_4_out, and_14_out, and_13_out);
  or or_5 (or_5_out, or_9_out, and_7_out);
  or or_6 (or_6_out, and_8_out, or_9_out);
  or or_7 (or_7_out, and_9_out, or_9_out);
  not not_11 (not_11_out, comparator_11_gt);
  not not_12 (not_12_out, comparator_12_gt);
  and and_12 (and_12_out, not_12_out, not_11_out);
  not not_13 (not_13_out, comparator_13_gt);
  Comparator #(.width(6), .mode("unsigned")) comparator_13 (
    .a(6'b110100), .b(random_2_out), .gt(comparator_13_gt));  // open: eq, lt
  not not_14 (not_14_out, comparator_14_gt);
  Comparator #(.width(6), .mode("unsigned")) comparator_14 (
    .a(random_2_out), .b(6'b111010), .gt(comparator_14_gt));  // open: eq, lt
  and and_13 (and_13_out, not_14_out, not_13_out);
  or or_8 (or_8_out, and_12_out, and_14_out, and_13_out);
  Comparator #(.width(6), .mode("unsigned")) comparator_15 (
    .a(6'b111011), .b(random_2_out), .gt(comparator_15_gt));  // open: eq, lt
  Comparator #(.width(6), .mode("unsigned")) comparator_16 (
    .a(random_2_out), .b({6{1'b1}}), .gt(comparator_16_gt));  // open: eq, lt
  or or_9 (or_9_out, and_13_out, and_12_out, and_10_out, and_14_out);
  not not_15 (not_15_out, comparator_15_gt);
  not not_16 (not_16_out, comparator_16_gt);
  buf and_14 (and_14_out, not_15_out);  // AND_Gate
  LED led_1 (.in(and_15_out));
  LED led_2 (.in(or_3_out));
  LED led_3 (.in(or_10_out));
  LED led_4 (.in(or_11_out));
  LED led_5 (.in(or_7_out));
  LED led_6 (.in(and_16_out));
  LED led_7 (.in(or_1_out));
  LED led_8 (.in(or_12_out));
  LED led_9 (.in(or_13_out));
  LED led_10 (.in(or_6_out));
  LED led_11 (.in(and_19_out));
  LED led_12 (.in(or_2_out));
  LED led_13 (.in(or_14_out));
  LED led_14 (.in(or_15_out));
  LED led_15 (.in(or_5_out));
  and and_15 (and_15_out, and_14_out, and_3_out);
  Clock clock_1 (.out(clock_1_out));
  and and_16 (and_16_out, and_2_out, and_14_out);
  and and_17 (and_17_out, and_12_out, and_3_out);
  and and_18 (and_18_out, and_3_out, and_10_out);
  or or_10 (or_10_out, or_4_out, and_17_out);
  or or_11 (or_11_out, and_18_out, or_8_out);
  Random #(.width(6)) random_2 (.clk(clock_1_out), .next(in_1), .out(random_2_out));  // open: clr
  and and_19 (and_19_out, and_14_out, and_1_out);
  or or_12 (or_12_out, or_4_out, and_20_out);
  and and_20 (and_20_out, and_12_out, and_2_out);
  and and_21 (and_21_out, and_2_out, and_10_out);
  and and_22 (and_22_out, and_12_out, and_1_out);
  and and_23 (and_23_out, and_1_out, and_10_out);
  or or_13 (or_13_out, and_21_out, and_21_out, or_8_out);
  or or_14 (or_14_out, or_4_out, and_22_out);
  or or_15 (or_15_out, and_23_out, or_8_out);

  // Notes on the sheet:
  //                  Amplitude
  //   3
  //   2
  //   1
  //   Frequency
  //                                         S V Karthikeya 231CS150
  //                                                     Tankasala Amith Teja  231CS159
  //                                                                           2. the output will be seen in the rgb area
  //                     Team ID: eternalumin48
  //                                               Tejavath Shashank 231CS160
  //          Instructions:
  //                                                                                                                                                                                    1. you can use given random number generator for frequency and amplitude inputs or use desired values
endmodule
